# Fritzing sketch sketch (saved by Fritzing 0.7.10b)
breadboards: 1

parts:
  Arduino_Ethernet_Shield1 = Arduino Ethernet Shield
  R1 = Photocell (LDR) [package=THT]
  LCD1 = LCD screen
  R2 = Resistor [tolerance=±5% resistance=10 package=THT]
  XTAL1 = CRYSTAL - kHz [frequency="1 MHz"]
  IC1 = IC, DIP package, 8 pins [chip_label=IC]

nets:
  N1: Arduino_Ethernet_Shield1.D9, LCD1.LED+
  N2: Arduino_Ethernet_Shield1.D7, LCD1.RS
  N3: Arduino_Ethernet_Shield1.D6, LCD1.E
  N4: Arduino_Ethernet_Shield1.D5, LCD1.DB4
  N5: Arduino_Ethernet_Shield1.SS, LCD1.DB5
  N6: Arduino_Ethernet_Shield1.D3, LCD1.DB6
  N7: Arduino_Ethernet_Shield1.D2, LCD1.DB7
  N8: Arduino_Ethernet_Shield1.A0, R1.pin_1, R2.Pin_0
  N9: Arduino_Ethernet_Shield1.A4, IC1.pin5
  N10: Arduino_Ethernet_Shield1.A5, IC1.pin6
  N11: LCD1.VSS, LCD1.V0, LCD1.LED-
  N12: LCD1.VDD, IC1.pin4
  N13: XTAL1.pin_0, IC1.pin2
  N14: XTAL1.pin_1, IC1.pin1
