# Fritzing sketch sketch2 (saved by Fritzing 0.7.10b)
breadboards: 1

parts:
  Arduino_Ethernet_Shield1 = Arduino Ethernet Shield
  LCD1 = LCD screen
  Part1 = Real Time Clock Module - DS1307 RTC Breakout Board
  R1 = Photocell (LDR) [package=THT]
  R2 = 10 Ω Resistor [package=THT]

nets:
  N1: Arduino_Ethernet_Shield1.D9, LCD1.LED+
  N2: Arduino_Ethernet_Shield1.D7, LCD1.RS
  N3: Arduino_Ethernet_Shield1.D6, LCD1.E
  N4: Arduino_Ethernet_Shield1.D5, LCD1.DB4
  N5: Arduino_Ethernet_Shield1.SS, LCD1.DB5
  N6: Arduino_Ethernet_Shield1.D3, LCD1.DB6
  N7: Arduino_Ethernet_Shield1.D2, LCD1.DB7
  N8: Arduino_Ethernet_Shield1.A0, R1.pin_1, R2.Pin_0
  N9: Arduino_Ethernet_Shield1.A4, Part1.SCL
  N10: Arduino_Ethernet_Shield1.A5, Part1.SDA
  VSS: LCD1.VSS, LCD1.V0, LCD1.R/W, LCD1.LED-, Part1.GND
  VDD: LCD1.VDD, Part1.5V
